# Fritzing sketch IoT-led-pbs (saved by Fritzing 1.0.2b)
breadboards: 1

parts:
  Resistor_(LED) = Resistor [tolerance=±5% resistance=220 package="2512 [SMD]"]
  Resistor_(PBS) = Resistor [tolerance=±5% resistance=220 package="2512 [SMD]"]
  Push-button_Switch_(PBS) = Pushbutton [package="[THT]"]
  LED = LED - 5mm [color="Red (633nm)" current=0.030A package="5 mm [THT]"]
  Teensy_3_2 = Teensy 3.2  # not connected

nets:
  N1: Resistor_(LED).Pin_1, LED.anode
  N2: Resistor_(PBS).Pin_0, Push-button_Switch_(PBS).Pin_1, Push-button_Switch_(PBS).Pin_2
  N3: Resistor_(PBS).Pin_1, LED.cathode
  N4: Push-button_Switch_(PBS).Pin_3, Push-button_Switch_(PBS).Pin_4

notes:
  CST8227 - Interfacing
  Internet of Things (IoT)
  Discrete LED with push-button switch (PBS) in pull-down configuration.
  Pins:
  3 (digital): push-button switch (PBS)
  15 (digital): discrete LED
  Instructions:
  1) Build this circuit.
  2) Upload 'Standard Firmata Plus' to your Teensy; *quit* Arduino IDE and Teensy Loader.
  3) Run node-red
  Gerald.Hurdle@AlgonquinCollege.com

custom parts:
  Teensy 3.2: The Teensy is a complete USB-based microcontoller development system, in a very small footprint, capable of implementing many types of projects. All programming is done via the USB port. No special programmer is needed, only a standard micro-USB cable and a PC or Macintosh with a USB port. It has a USB keyboard/mouse/joystick emulation stack and can be programmed through Arduino IDE.
