# Fritzing sketch board-setup (saved by Fritzing 1.0.2b)
breadboards: 1

parts:
  A1 = Teensy 4.0
  S1 = Pushbutton [package="[THT]"]
  S2 = Pushbutton [package="[THT]"]
  R1 = Resistor [tolerance=±5% power=0.25W resistance=10k package=THT]
  R2 = Resistor [tolerance=±5% power=0.25W resistance=220 package=THT]
  R3 = Resistor [tolerance=±5% power=0.25W resistance=220 package=THT]
  R4 = Resistor [tolerance=±5% power=0.25W resistance=220 package=THT]
  LED1 = RGB LED (com. cathode, rgb) [color="Red (633nm)" current=0.030A package="5 mm [THT]"]

nets:
  N1: A1.pin_1, A1.pin_32, S1.Pin_1, S1.Pin_2, S2.Pin_1, S2.Pin_2, LED1.common_cathode
  N2: A1.pin_9, S1.Pin_3, S1.Pin_4, R1.Pin_1
  N3: A1.pin_10, S2.Pin_3, S2.Pin_4
  N4: A1.pin_21, R2.Pin_0
  N5: A1.pin_22, R3.Pin_0
  N6: A1.pin_25, R4.Pin_0
  N7: A1.pin_31, R1.Pin_0
  N8: R2.Pin_1, LED1.blue_anode
  N9: R3.Pin_1, LED1.green_anode
  N10: R4.Pin_1, LED1.red_anode

custom parts:
  Teensy 4.0: The Teensy is a complete USB-based microcontoller development system, in a very small footprint, capable of implementing many types of projects. All programming is done via the USB port. No special programmer is needed, only a standard micro-USB cable and a PC or Macintosh with a USB port. (Oct 2023 added the VBUS pad at user request.)
